# Fritzing sketch powerboard_ampel (saved by Fritzing 0.9.3b)
circuit board: 3.54996cm x 1.18795cm

parts:
  SCL = Header 12 [package=1x12_machine-pin-header_lock.004]
  SDA = Header 12 [package=1x12_machine-pin-header_lock.004]
  GND = Header 12 [package=1x12_machine-pin-header_lock.004]
  5V = Header 12 [package=1x12_machine-pin-header_lock.004]

nets:
  N1: SCL.1, SCL.2, SCL.3, SCL.4, SCL.5, SCL.6, SCL.7, SCL.8, SCL.9, SCL.10, SCL.11, SCL.12
  N2: SDA.1, SDA.2, SDA.3, SDA.4, SDA.5, SDA.6, SDA.7, SDA.8, SDA.9, SDA.10, SDA.11, SDA.12
  N3: GND.1, GND.2, GND.3, GND.4, GND.5, GND.6, GND.7, GND.8, GND.9, GND.10, GND.11, GND.12
  N4: 5V.1, 5V.2, 5V.3, 5V.4, 5V.5, 5V.6, 5V.7, 5V.8, 5V.9, 5V.10, 5V.11, 5V.12
